# Fritzing sketch Board for Project Schematic (saved by Fritzing 0.9.3b)
breadboards: 1

parts:
  J2 = LOAD_CELL [package=1x03]
  Part7 = HX711 Weighing Sensor Module
  Part8 = Arduino Pro Mini (5V)
  Part9 = Adafruit 1.44 inch TFT Breakout [part_number="Adafruit #2088"]
  S5 = Pushbutton [part_number=COM-09190 package="[THT]"]
  S6 = Pushbutton [part_number=COM-09190 package="[THT]"]
  S7 = Pushbutton [part_number=COM-09190 package="[THT]"]
  S8 = Pushbutton [part_number=COM-09190 package="[THT]"]
  R5 = Resistor [tolerance=±5% resistance=10k package=THT]
  R6 = Resistor [tolerance=±5% resistance=10k package=THT]
  R7 = Resistor [tolerance=±5% resistance=10k package=THT]
  R8 = Resistor [tolerance=±5% resistance=10k package=THT]
  Part10 = PowerBoost 500 Charger
  U4 = SWITCH_SPDT [package=kps-1290]
  U3 = LIPO-1000mAh [package=lipo-1000]

nets:
  N1: J2.B, Part7.E+
  N2: J2.W, Part7.E-
  N3: J2.R, Part7.A-
  VCC: Part7.VCC, Part8.VCC, Part9.VIN, Part10.VBAT, U4.S
  GND: Part7.GND, Part8.GND, Part9.GND, R5.Pin_1, R6.Pin_1, R7.Pin_1, R8.Pin_1, Part10.GND, U4.O, U4.P, U3.-
  N4: Part8.SCK, Part9.SCK
  N5: Part8.MOSI, Part9.MOSI
  N6: Part8.D10, Part9.TFTCS
  N7: Part8.D9, Part9.RESET
  N8: Part8.D8, Part9.TFTDC
  N9: Part8.D7, S8.Pin_3, S8.Pin_4
  N10: Part8.D6, S7.Pin_3, S7.Pin_4
  N11: Part8.D5, S6.Pin_3, S6.Pin_4
  N12: Part8.D3, S5.Pin_3, S5.Pin_4
  N13: S5.Pin_1, S5.Pin_2, R7.Pin_0
  N14: S6.Pin_1, S6.Pin_2, R6.Pin_0
  N15: S7.Pin_1, S7.Pin_2, R5.Pin_0
  N16: S8.Pin_1, S8.Pin_2, R8.Pin_0
  N17: Part10.5.0V, U3.+

custom parts:
  Adafruit 1.44 inch TFT Breakout: This lovely little display breakout is the best way to add a small, colorful and bright display to any project. Since the display uses 4-wire SPI to communicate and has its own pixel-addressable frame buffer, it can be used with every kind of microcontroller. Even a very small one with low memory and few pins available! The 1.44" display has 128x128 color pixels. Unlike the low cost "Nokia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
  Pushbutton: A generic pushbutton. This is a standard 12mm square momentary button. What we really like is the large button head and good tactile feel (it ‘clicks’ really well). This button is great for user input on a PCB or a good, big reset button on a breadboard. Breadboard friendly! SparkFun Storefront SKU: COM-09190 Modified by: Ho Yun "Bobby" Chan @ SparkFun Electronics Inc.
  PowerBoost 500 Charger: The PowerBoost 500C is a little DC/DC boost converter module that can be powered by any 3.7V LiIon/LiPoly battery, and convert the battery output to 5.2V DC for running your 5V projects. At its heart is a TPS61090 boost converter from TI. This boost converter chip has some really nice extras such as low battery detection, 2A internal switch, synchronous conversion, excellent efficiency, and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
