# Fritzing sketch Board for project PCB (saved by Fritzing 0.9.3b)
circuit board: 3.5cm x 6cm
circuit board: 5cm x 3cm
circuit board: 6.70177cm x 3.84414cm
circuit board: 7.46cm x 5.03767cm
breadboards: 1

parts:
  Part7 = HX711 Weighing Sensor Module
  Part8 = Arduino Pro Mini (5V)
  Part9 = Adafruit 1.44 inch TFT Breakout [part_number="Adafruit #2088"]
  S5 = Pushbutton [part_number=COM-09190 package="[THT]"]
  S6 = Pushbutton [part_number=COM-09190 package="[THT]"]
  S7 = Pushbutton [part_number=COM-09190 package="[THT]"]
  S8 = Pushbutton [part_number=COM-09190 package="[THT]"]
  R5 = Resistor [tolerance=±5% resistance=10k package=THT]
  R6 = Resistor [tolerance=±5% resistance=10k package=THT]
  R7 = Resistor [tolerance=±5% resistance=10k package=THT]
  R8 = Resistor [tolerance=±5% resistance=10k package=THT]
  Part10 = PowerBoost 500 Charger
  U4 = SWITCH_SPDT [package=kps-1290]
  Part12 = Arduino Pro Mini (5V)  # not connected
  UP = Pushbutton [part_number=COM-09190 package="[THT]"]
  HOME = Pushbutton [part_number=COM-09190 package="[THT]"]
  R9 = Resistor [tolerance=±5% resistance=10k package=THT]
  R10 = Resistor [tolerance=±5% resistance=10k package=THT]
  DOWN = Pushbutton [part_number=COM-09190 package="[THT]"]
  SELECT = Pushbutton [part_number=COM-09190 package="[THT]"]
  U_S_D_H_G = Resistor [tolerance=±5% resistance=10k package=THT]
  BUTTONS = female pin header, 5 pins [form="♀ (female)"]
  R11 = Resistor [tolerance=±5% resistance=10k package=THT]
  WGH_SENSOR = HX711 Weighing Sensor Module
  ARDUINO = female pin header, 12 pins [form="♀ (female)"]
  ARDUINO_2 = female pin header, 12 pins [form="♀ (female)"]
  SCREEN_HEADER = female pin header, 11 pins [form="♀ (female)"]
  U_S_D_H_G_2 = female pin header, 5 pins [form="♀ (female)"]
  U5 = LIPO-1000mAh [package=lipo-1000]  # not connected

nets:
  VCC: Part7.VCC, Part8.RAW, Part9.VIN
  GND: Part7.GND, Part8.GND, Part9.GND, R5.Pin_1, R6.Pin_1, R7.Pin_1, R8.Pin_1, Part10.GND, U4.P, U4.S
  N1: Part7.DO/RX, Part8.A1
  N2: Part7.CK/TX, Part8.A0
  N3: Part8.SCK, Part9.SCK
  N4: Part8.MOSI, Part9.MOSI
  N5: Part8.D10, Part9.TFTCS
  N6: Part8.D9, Part9.RESET
  N7: Part8.D8, Part9.TFTDC
  N8: Part8.D7, S7.Pin_1, S7.Pin_2
  N9: Part8.D6, S8.Pin_1, S8.Pin_2
  N10: Part8.D5, S5.Pin_1, S5.Pin_2
  N11: Part8.D4, S6.Pin_1, S6.Pin_2
  N12: S5.Pin_3, R7.Pin_0
  N13: S6.Pin_3, R6.Pin_0
  N14: S7.Pin_3, S7.Pin_4, R5.Pin_0
  N15: S8.Pin_3, R8.Pin_0
  N16: Part10.5.0V, U4.O
  N17: UP.Pin_1, UP.Pin_2, BUTTONS.pin1
  N18: UP.Pin_3, R9.Pin_1
  N19: HOME.Pin_1, HOME.Pin_2, BUTTONS.pin4
  N20: HOME.Pin_3, U_S_D_H_G.Pin_1
  N21: R9.Pin_0, R10.Pin_0, U_S_D_H_G.Pin_0, BUTTONS.pin5, R11.Pin_0
  N22: R10.Pin_1, SELECT.Pin_3
  N23: DOWN.Pin_2, BUTTONS.pin3
  N24: DOWN.Pin_3, DOWN.Pin_4, R11.Pin_1
  N25: SELECT.Pin_1, SELECT.Pin_2, BUTTONS.pin2
  N26: WGH_SENSOR.VCC, ARDUINO.pin1, SCREEN_HEADER.pin1
  N27: WGH_SENSOR.GND, ARDUINO.pin2, SCREEN_HEADER.pin3, U_S_D_H_G_2.pin5
  N28: WGH_SENSOR.DO/RX, ARDUINO.pin7
  N29: WGH_SENSOR.CK/TX, ARDUINO.pin8
  N30: ARDUINO.pin9, SCREEN_HEADER.pin4
  N31: ARDUINO.pin11, SCREEN_HEADER.pin6
  N32: ARDUINO.pin12, SCREEN_HEADER.pin7
  N33: ARDUINO_2.pin7, U_S_D_H_G_2.pin1
  N34: ARDUINO_2.pin8, U_S_D_H_G_2.pin2
  N35: ARDUINO_2.pin9, U_S_D_H_G_2.pin3
  N36: ARDUINO_2.pin10, U_S_D_H_G_2.pin4
  N37: ARDUINO_2.pin11, SCREEN_HEADER.pin9
  N38: ARDUINO_2.pin12, SCREEN_HEADER.pin8

custom parts:
  Adafruit 1.44 inch TFT Breakout: This lovely little display breakout is the best way to add a small, colorful and bright display to any project. Since the display uses 4-wire SPI to communicate and has its own pixel-addressable frame buffer, it can be used with every kind of microcontroller. Even a very small one with low memory and few pins available! The 1.44" display has 128x128 color pixels. Unlike the low cost "Nokia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
  Pushbutton: A generic pushbutton. This is a standard 12mm square momentary button. What we really like is the large button head and good tactile feel (it ‘clicks’ really well). This button is great for user input on a PCB or a good, big reset button on a breadboard. Breadboard friendly! SparkFun Storefront SKU: COM-09190 Modified by: Ho Yun "Bobby" Chan @ SparkFun Electronics Inc.
  PowerBoost 500 Charger: The PowerBoost 500C is a little DC/DC boost converter module that can be powered by any 3.7V LiIon/LiPoly battery, and convert the battery output to 5.2V DC for running your 5V projects. At its heart is a TPS61090 boost converter from TI. This boost converter chip has some really nice extras such as low battery detection, 2A internal switch, synchronous conversion, excellent efficiency, and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
