# Fritzing sketch Board for project (saved by Fritzing 0.9.3b)
breadboards: 1

parts:
  Part3 = HX711 Weighing Sensor Module
  Part4 = Arduino Pro Mini (5V)
  Part5 = Adafruit 1.44 inch TFT Breakout [part_number="Adafruit #2088"]
  S1 = Pushbutton [part_number=COM-09190 package="[THT]"]
  S2 = Pushbutton [part_number=COM-09190 package="[THT]"]
  S3 = Pushbutton [part_number=COM-09190 package="[THT]"]
  R1 = Resistor [tolerance=±5% resistance=10k package=THT]
  R2 = Resistor [tolerance=±5% resistance=10k package=THT]
  R3 = Resistor [tolerance=±5% resistance=10k package=THT]
  R4 = Resistor [tolerance=±5% resistance=10k package=THT]
  S4 = Pushbutton [part_number=COM-09190 package="[THT]"]
  U1 = LIPO-1000mAh [package=lipo-1000]
  Part6 = PowerBoost 500 Charger
  U2 = SWITCH_SPDT [package=kps-1290]
  J1 = LOAD_CELL [package=1x03]

nets:
  VCC: Part3.VCC, Part4.RAW, Part5.VIN, U1.+, Part6.5.0V, U2.O
  GND: Part3.GND, Part4.GND, Part5.GND, R1.Pin_1, R2.Pin_1, R3.Pin_1, R4.Pin_1, U1.-, Part6.GND, U2.P, U2.S
  N1: Part3.DO/RX, Part4.A1
  N2: Part3.CK/TX, Part4.A0
  N3: Part3.E+, J1.R
  N4: Part3.E-, J1.W
  N5: Part3.A+, J1.B
  N6: Part4.SCK, Part5.SCK
  N7: Part4.MOSI, Part5.MOSI
  N8: Part4.D10, Part5.TFTCS
  N9: Part4.D9, Part5.RESET
  N10: Part4.D8, Part5.TFTDC
  N11: Part4.D7, R1.Pin_0, S4.Pin_3, S4.Pin_4
  N12: Part4.D6, S3.Pin_3, S3.Pin_4, R4.Pin_0
  N13: Part4.D5, S2.Pin_3, S2.Pin_4, R3.Pin_0
  N14: Part4.D3, S1.Pin_3, S1.Pin_4, R2.Pin_0
  N15: S1.Pin_1, S1.Pin_2
  N16: S2.Pin_1, S2.Pin_2
  N17: S3.Pin_1, S3.Pin_2
  N18: S4.Pin_1, S4.Pin_2

custom parts:
  Adafruit 1.44 inch TFT Breakout: This lovely little display breakout is the best way to add a small, colorful and bright display to any project. Since the display uses 4-wire SPI to communicate and has its own pixel-addressable frame buffer, it can be used with every kind of microcontroller. Even a very small one with low memory and few pins available! The 1.44" display has 128x128 color pixels. Unlike the low cost "Nokia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
  Pushbutton: A generic pushbutton. This is a standard 12mm square momentary button. What we really like is the large button head and good tactile feel (it ‘clicks’ really well). This button is great for user input on a PCB or a good, big reset button on a breadboard. Breadboard friendly! SparkFun Storefront SKU: COM-09190 Modified by: Ho Yun "Bobby" Chan @ SparkFun Electronics Inc.
  PowerBoost 500 Charger: The PowerBoost 500C is a little DC/DC boost converter module that can be powered by any 3.7V LiIon/LiPoly battery, and convert the battery output to 5.2V DC for running your 5V projects. At its heart is a TPS61090 boost converter from TI. This boost converter chip has some really nice extras such as low battery detection, 2A internal switch, synchronous conversion, excellent efficiency, and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
